# Fritzing sketch Winder (saved by Fritzing 0.9.3b)

parts:
  Componente2 = Arduino Nano (Rev3.0) (ICSP)
  MOTOR1 = 28BYJ-48 Stepper Motor
  BREAKOUT1 = ULN2003A breakout board

nets:
  N1: Componente2.GND, BREAKOUT1.0V
  N2: Componente2.D8, BREAKOUT1.In_4
  N3: Componente2.D9, BREAKOUT1.In_3
  N4: Componente2.D10, BREAKOUT1.In_2
  N5: Componente2.D11/MOSI, BREAKOUT1.In_1
  5V: Componente2.5V, BREAKOUT1.+5V
  N6: MOTOR1.RED, BREAKOUT1.RED_wire
  N7: MOTOR1.ORANGE, BREAKOUT1.ORANGE_wire
  N8: MOTOR1.YELLOW, BREAKOUT1.YELLOW_wire
  N9: MOTOR1.PINK, BREAKOUT1.PINK_wire
  N10: MOTOR1.BLUE, BREAKOUT1.BLUE_wire

custom parts:
  ULN2003A breakout board: ULN2003A 7-way Darlington Transistor Driver on breakoutboard
